// Logisim project DragonArch.circ as structural Verilog: 8 circuits, main circuit main
module main (
  input  PCReset
);

  wire _0_out, _1_out, _2_out, _3_out, _4_out, _5_out, _6_out, _7_out, _8_out, _9_out, button_2_out,
       button_out, clock_1_out, clock_2_out, DataWrite, ImLoad, IRLoad, led16_1_out_2, led16_1_out_3,
       led16_1_out_4, led16_1_out_5, led16_1_out_6, led16_1_out_7, led16_1_out_8, led16_1_out_9,
       led16_1_out_10, led16_1_out_11, led16_1_out_12, led16_1_out_13, led16_1_out_14, led16_1_out_15,
       led16_1_out_16, led16_1_out_17, not_1_out, PCLoad, Write0, Write1, Write2;
  wire [1:0] AddrSelect, DataSelect, Op2Sel, PCSellect, RegSrc;
  wire [2:0] ir_1_registerselect0, ir_1_registerselect1, ir_1_registerselect2;
  wire [3:0] ALUCode, Opcode;
  wire [7:0] cu_1_ucounter;
  wire [15:0] ALUOut, gprs_1_registerout0, gprs_1_registerout1, gprs_1_registerout2, gprs_1_registerout3,
       gprs_1_registerout4, gprs_1_registerout5, gprs_1_registerout6, gprs_1_registerout7, Immed,
       multiplexer_1_out, multiplexer_2_out, multiplexer_3_out, multiplexer_4_out, PC, pc_1_pcout,
       ram_1_data, Read0, Read1, Read2, S_Register;

  LED led_1 (.in(led16_1_out_4));
  LED led_2 (.in(led16_1_out_2));
  LED led_3 (.in(led16_1_out_3));
  LED led_4 (.in(led16_1_out_5));
  LED led_5 (.in(led16_1_out_10));
  LED led_6 (.in(led16_1_out_12));
  LED led_7 (.in(led16_1_out_13));
  LED led_8 (.in(led16_1_out_11));
  LED led_9 (.in(led16_1_out_7));
  LED led_10 (.in(led16_1_out_8));
  LED led_11 (.in(led16_1_out_6));
  LED led_12 (.in(led16_1_out_9));
  LED led_13 (.in(led16_1_out_15));
  LED led_14 (.in(led16_1_out_16));
  LED led_15 (.in(led16_1_out_14));
  LED led_16 (.in(led16_1_out_17));
  Led16 led16_1 (
    .in_1(multiplexer_1_out), .out_2(led16_1_out_2), .out_3(led16_1_out_3), .out_4(led16_1_out_4),
    .out_5(led16_1_out_5), .out_6(led16_1_out_6), .out_7(led16_1_out_7), .out_8(led16_1_out_8),
    .out_9(led16_1_out_9), .out_10(led16_1_out_10), .out_11(led16_1_out_11), .out_12(led16_1_out_12),
    .out_13(led16_1_out_13), .out_14(led16_1_out_14), .out_15(led16_1_out_15), .out_16(led16_1_out_16),
    .out_17(led16_1_out_17));
  // Probe on multiplexer_1_out
  Clock clock_1 (.out(clock_1_out));
  RAM #(.addrWidth(16), .dataWidth(16)) ram_1 (
    .addr(multiplexer_1_out), .data(ram_1_data), .clk(clock_1_out), .ld(not_1_out));  // open: sel, clr
  not not_1 (not_1_out, DataWrite);
  // Probe on cu_1_ucounter
  CU cu_1 (
    .ucounter(cu_1_ucounter), .opcode(Opcode), .aluop(ALUCode), .op2sel(Op2Sel), .datawrite(DataWrite),
    .addrsel(AddrSelect), .pcsel(PCSellect), .pcload(PCLoad), .dwrite(Write2), .irload(IRLoad),
    .imload(ImLoad), .regsrc(RegSrc), .datasel(DataSelect), .swrite(Write1));  // open: z, n, c
  Multiplexer #(.select(2), .width(16), .enable("false")) multiplexer_1 (
    .in0(pc_1_pcout), .in1(Immed), .in2(ALUOut), .in3(S_Register), .out(multiplexer_1_out), .sel(AddrSelect));
  // Probe on ram_1_data
  // Probe on pc_1_pcout
  assign ram_1_data = DataWrite ? multiplexer_2_out : 16'bz;  // Controlled_Buffer controlled_buffer_1
  Clock clock_2 (.out(clock_2_out));
  Multiplexer #(.select(2), .width(16), .enable("false")) multiplexer_2 (
    .in0(PC), .in1(Read0), .in2(Read1), .in3(ALUOut), .out(multiplexer_2_out), .sel(DataSelect));
  PC pc_1 (
    .ImmidiateRegister(Immed), .S_Register(S_Register), .PCOut(pc_1_pcout), .PCSelect(PCSellect),
    .PCLoad(PCLoad), .PCReset(PCReset));
  Register #(.width(16)) register_1 (.D(ram_1_data), .en(ImLoad), .Q(Immed), .clk(clock_2_out));  // open: clr
  Button _1 (.out(_1_out));
  Button _4 (.out(_4_out));
  Button _7 (.out(_7_out));
  Button button (.out(button_out));
  IR ir_1 (
    .IRLoad(IRLoad), .instruction(ram_1_data), .Opcode(Opcode), .RegisterSelect0(ir_1_registerselect0),
    .RegisterSelect1(ir_1_registerselect1), .RegisterSelect2(ir_1_registerselect2));
  Button _3 (.out(_3_out));
  Button _2 (.out(_2_out));
  Button _5 (.out(_5_out));
  Button _6 (.out(_6_out));
  Button _9 (.out(_9_out));
  Button _8 (.out(_8_out));
  Button button_2 (.out(button_2_out));
  Button _0 (.out(_0_out));
  Multiplexer #(.select(2), .width(16), .enable("false")) multiplexer_3 (
    .in0(ram_1_data), .in1(Immed), .in2(ALUOut), .in3(S_Register), .out(multiplexer_3_out), .sel(RegSrc));
  Keypad keypad_1 (
    .digit0(_0_out), .digit1(_1_out), .digit2(_2_out), .digit3(_3_out), .digit4(_4_out), .digit5(_5_out),
    .digit6(_6_out), .digit7(_7_out), .digit8(_8_out), .digit9(_9_out), .op_star(button_out),
    .nop(button_2_out));  // open: digit, isdigit, is_star, nis, press
  GPRs gprs_1 (
    .Select0(ir_1_registerselect2), .RegisterIn(multiplexer_3_out), .RegisterOut0(gprs_1_registerout0),
    .RegisterOut1(gprs_1_registerout1), .RegisterOut2(gprs_1_registerout2),
    .RegisterOut3(gprs_1_registerout3), .RegisterOut4(gprs_1_registerout4),
    .RegisterOut5(gprs_1_registerout5), .RegisterOut6(gprs_1_registerout6),
    .RegisterOut7(gprs_1_registerout7), .Write0(Write0), .Write1(Write1), .Write2(Write2), .Read0(Read0),
    .Read1(Read2), .Read3(Read1), .Select1(ir_1_registerselect1), .Select2(ir_1_registerselect0));
  // Probe on gprs_1_registerout0
  // Probe on gprs_1_registerout1
  // Probe on gprs_1_registerout2
  // Probe on gprs_1_registerout3
  // Probe on gprs_1_registerout4
  // Probe on gprs_1_registerout5
  // Probe on gprs_1_registerout6
  // Probe on gprs_1_registerout7
  // Probe on ALUOut
  Multiplexer #(.select(2), .width(16), .enable("false")) multiplexer_4 (
    .in0(Read2), .in1(Immed), .in2({16{1'b0}}), .in3(16'h1), .out(multiplexer_4_out), .sel(Op2Sel));
  ALU alu_1 (.X(Read1), .Y(multiplexer_4_out), .Out(ALUOut), .ALU_code(ALUCode));

  // Notes on the sheet:
  //   Immediate Register
  //   Dragon Architecture 16-bit CPU
endmodule

module ALU (
  input  [3:0] ALU_code,
  input  [15:0] X,
  input  [15:0] Y,
  output [15:0] Out
);

  wire adder_1_cout, adder_2_cout, multiplexer_2_out, subtractor_1_bout, subtractor_2_bout, undriven;
  wire [1:0] undriven_2;
  wire [15:0] adder_1_out, adder_2_out, and_1_out, negator_1_out, or_1_out, subtractor_1_out,
       subtractor_2_out, xor_1_out;

  Adder #(.width(16)) adder_1 (.a(X), .b(X), .out(adder_1_out), .cin(undriven), .cout(adder_1_cout));
  Subtractor #(.width(16)) subtractor_1 (
    .a(X), .b(X), .out(subtractor_1_out), .bin(undriven), .bout(subtractor_1_bout));
  assign and_1_out = X & X;  // AND_Gate and_1, 16 bits wide
  assign or_1_out = X | X;  // OR_Gate or_1, 16 bits wide
  assign xor_1_out = X ^ X;  // XOR_Gate xor_1, 16 bits wide
  Negator #(.width(16)) negator_1 (.in(X), .out(negator_1_out));
  Adder #(.width(16)) adder_2 (.a(X), .b(16'h1), .out(adder_2_out), .cin(undriven), .cout(adder_2_cout));
  Subtractor #(.width(16)) subtractor_2 (
    .a(X), .b(16'h1), .out(subtractor_2_out), .bin(undriven), .bout(subtractor_2_bout));
  Multiplexer #(.select(4), .width(16), .enable("false")) multiplexer_1 (
    .in0(adder_1_out), .in1(subtractor_1_out), .in2(and_1_out), .in3(or_1_out), .in4(xor_1_out),
    .in5(negator_1_out), .in6(X), .in7(adder_2_out), .in8(subtractor_2_out), .out(Out), .sel(ALU_code));  // open: in9, in10, in11, in12, in13, in14, in15
  Multiplexer #(.select(2), .enable("false")) multiplexer_2 (
    .in0(adder_1_cout), .in1(subtractor_1_bout), .in2(adder_2_cout), .in3(subtractor_2_bout),
    .out(multiplexer_2_out), .sel(undriven_2));

  assign Y = X;

  // Notes on the sheet:
  //   CarryIn???
  //   Arithmetic Logic Unit
  //   ???
  //   ???
  //   CarryOut???
endmodule

module GPRs (
  input  Write0,
  input  Write1,
  input  Write2,
  input  [2:0] Select2,
  input  [2:0] Select1,
  input  [2:0] Select0,
  input  [15:0] RegisterIn,
  output [15:0] Read0,
  output [15:0] Read1,
  output [15:0] Read3,
  output [15:0] RegisterOut0,
  output [15:0] RegisterOut1,
  output [15:0] RegisterOut2,
  output [15:0] RegisterOut3,
  output [15:0] RegisterOut4,
  output [15:0] RegisterOut5,
  output [15:0] RegisterOut6,
  output [15:0] RegisterOut7
);

  wire Clock_out, demultiplexer_1_out0, demultiplexer_1_out1, demultiplexer_1_out2, demultiplexer_1_out3,
       demultiplexer_1_out4, demultiplexer_1_out5, demultiplexer_1_out6, demultiplexer_1_out7;

  Demultiplexer #(.select(3), .enable("false")) demultiplexer_1 (
    .out0(demultiplexer_1_out0), .out1(demultiplexer_1_out1), .out2(demultiplexer_1_out2),
    .out3(demultiplexer_1_out3), .out4(demultiplexer_1_out4), .out5(demultiplexer_1_out5),
    .out6(demultiplexer_1_out6), .out7(demultiplexer_1_out7), .in(Write0), .sel(Select0));
  Demultiplexer #(.select(3), .enable("false")) demultiplexer_2 (
    .out0(demultiplexer_1_out0), .out1(demultiplexer_1_out1), .out2(demultiplexer_1_out2),
    .out3(demultiplexer_1_out3), .out4(demultiplexer_1_out4), .out5(demultiplexer_1_out5),
    .out6(demultiplexer_1_out6), .out7(demultiplexer_1_out7), .in(Write1), .sel(Select1));
  Demultiplexer #(.select(3), .enable("false")) demultiplexer_3 (
    .out0(demultiplexer_1_out0), .out1(demultiplexer_1_out1), .out2(demultiplexer_1_out2),
    .out3(demultiplexer_1_out3), .out4(demultiplexer_1_out4), .out5(demultiplexer_1_out5),
    .out6(demultiplexer_1_out6), .out7(demultiplexer_1_out7), .in(Write2), .sel(Select2));
  Register #(.width(16)) Reg0 (
    .D(RegisterIn), .en(demultiplexer_1_out0), .Q(RegisterOut0), .clk(Clock_out));  // open: clr
  Register #(.width(16)) Reg1 (
    .D(RegisterIn), .en(demultiplexer_1_out1), .Q(RegisterOut1), .clk(Clock_out));  // open: clr
  Register #(.width(16)) Reg2 (
    .D(RegisterIn), .en(demultiplexer_1_out2), .Q(RegisterOut2), .clk(Clock_out));  // open: clr
  Register #(.width(16)) Reg3 (
    .D(RegisterIn), .en(demultiplexer_1_out3), .Q(RegisterOut3), .clk(Clock_out));  // open: clr
  Register #(.width(16)) Reg4 (
    .D(RegisterIn), .en(demultiplexer_1_out4), .Q(RegisterOut4), .clk(Clock_out));  // open: clr
  Register #(.width(16)) Reg5 (
    .D(RegisterIn), .en(demultiplexer_1_out5), .Q(RegisterOut5), .clk(Clock_out));  // open: clr
  Register #(.width(16)) Reg6 (
    .D(RegisterIn), .en(demultiplexer_1_out6), .Q(RegisterOut6), .clk(Clock_out));  // open: clr
  Register #(.width(16)) Reg7 (
    .D(RegisterIn), .en(demultiplexer_1_out7), .Q(RegisterOut7), .clk(Clock_out));  // open: clr
  Clock Clock (.out(Clock_out));
  Multiplexer #(.select(3), .width(16), .enable("false")) multiplexer_1 (
    .in0(RegisterOut0), .in1(RegisterOut1), .in2(RegisterOut2), .in3(RegisterOut3), .in4(RegisterOut4),
    .in5(RegisterOut5), .in6(RegisterOut6), .in7(RegisterOut7), .out(Read0), .sel(Select0));
  Multiplexer #(.select(3), .width(16), .enable("false")) multiplexer_2 (
    .in0(RegisterOut0), .in1(RegisterOut1), .in2(RegisterOut2), .in3(RegisterOut3), .in4(RegisterOut4),
    .in5(RegisterOut5), .in6(RegisterOut6), .in7(RegisterOut7), .out(Read1), .sel(Select1));
  Multiplexer #(.select(3), .width(16), .enable("false")) multiplexer_3 (
    .in0(RegisterOut0), .in1(RegisterOut1), .in2(RegisterOut2), .in3(RegisterOut3), .in4(RegisterOut4),
    .in5(RegisterOut5), .in6(RegisterOut6), .in7(RegisterOut7), .out(Read3), .sel(Select2));

  // Notes on the sheet:
  //   General Purpose Registers
endmodule

module IR (
  input  IRLoad,
  input  [15:0] instruction,
  output [3:0] Opcode,
  output [2:0] RegisterSelect0,
  output [2:0] RegisterSelect1,
  output [2:0] RegisterSelect2
);

  wire clock_1_out;
  wire [15:13] IR_q;

  Clock clock_1 (.out(clock_1_out));
  Register #(.width(16)) IR (
    .D(instruction), .en(IRLoad), .Q({IR_q, Opcode, RegisterSelect2, RegisterSelect1, RegisterSelect0}),
    .clk(clock_1_out));  // open: clr

  // Notes on the sheet:
  //   Instruction Register
endmodule

module PC (
  input  [15:0] ImmidiateRegister,
  input  PCLoad,
  input  PCReset,
  input  [15:0] S_Register,
  input  [1:0] PCSelect,
  output [15:0] PCOut
);

  wire clock_1_out;
  wire [15:0] adder_1_out, adder_2_out, multiplexer_1_out;

  Adder #(.width(16)) adder_1 (.a(PCOut), .b(16'h1), .out(adder_1_out));  // open: cin, cout
  Adder #(.width(16)) adder_2 (.a(PCOut), .b(ImmidiateRegister), .out(adder_2_out));  // open: cin, cout
  Multiplexer #(.select(2), .width(16), .enable("false")) multiplexer_1 (
    .in0(adder_1_out), .in1(ImmidiateRegister), .in2(adder_2_out), .in3(S_Register), .out(multiplexer_1_out),
    .sel(PCSelect));
  Clock clock_1 (.out(clock_1_out));
  Register #(.width(16)) PCReg (.D(multiplexer_1_out), .en(PCLoad), .Q(PCOut), .clk(clock_1_out), .clr(PCReset));

  // Notes on the sheet:
  //   Program Counter
endmodule

module CU (
  input  z,
  input  n,
  input  c,
  input  [3:0] opcode,
  output [3:0] aluop,
  output [1:0] op2sel,
  output datawrite,
  output [7:0] ucounter,
  output [1:0] addrsel,
  output [1:0] pcsel,
  output pcload,
  output dwrite,
  output irload,
  output imload,
  output [1:0] regsrc,
  output [1:0] datasel,
  output swrite
);

  wire clock_1_out, indexsel, multiplexer_2_out, or_1_out;
  wire [1:0] cond;
  wire [7:0] adder_1_out, multiplexer_1_out, multiplexer_3_out;
  wire [15:0] rom_2_data;
  wire [31:23] rom_1_data;

  Register Microcounter (.D(adder_1_out), .Q(ucounter), .clk(clock_1_out));  // open: en, clr
  Clock clock_1 (.out(clock_1_out));
  ROM #(.dataWidth(32)) rom_1 (
    .addr(ucounter),
    .data({rom_1_data, swrite, datasel, indexsel, cond, regsrc, imload, irload, dwrite, pcload, pcsel, addrsel, datawrite, op2sel, aluop}));  // open: sel
  ROM #(.dataWidth(16)) rom_2 (.addr(ucounter), .data(rom_2_data));  // open: sel
  or or_1 (or_1_out, z, n);
  Multiplexer #(.width(8), .enable("false")) multiplexer_1 (
    .in0(rom_2_data[7:0]), .in1(rom_2_data[15:8]), .out(multiplexer_1_out), .sel(multiplexer_2_out));
  Multiplexer #(.select(2), .enable("false")) multiplexer_2 (
    .in0(z), .in1(or_1_out), .in2(n), .in3(c), .out(multiplexer_2_out), .sel(cond));
  Multiplexer #(.width(8), .enable("false")) multiplexer_3 (
    .in0({8{1'b0}}), .in1({4'b0000, opcode}), .out(multiplexer_3_out), .sel(indexsel));
  Adder adder_1 (.a(multiplexer_1_out), .b(multiplexer_3_out), .out(adder_1_out));  // open: cin, cout

  // Notes on the sheet:
  //   Control Unit
  //   Control ROM
  //   Decision ROM
endmodule

module Keypad (
  input  digit0,
  input  digit1,
  input  digit2,
  input  digit3,
  input  digit4,
  input  digit5,
  input  digit6,
  input  digit7,
  input  digit8,
  input  digit9,
  input  op_star,
  input  nop,
  output [3:0] digit,
  output isdigit,
  output is_star,
  output nis,
  output press
);

  wire buffer_1_out, buffer_2_out, buffer_3_out, buffer_4_out, buffer_5_out, buffer_6_out, buffer_7_out,
       buffer_8_out, buffer_9_out, buffer_10_out, buffer_11_out, buffer_12_out, buffer_13_out, buffer_14_out,
       buffer_15_out, buffer_16_out, buffer_17_out, buffer_18_out, buffer_19_out, buffer_20_out,
       buffer_21_out, buffer_22_out, buffer_23_out, buffer_24_out, buffer_25_out, buffer_26_out,
       buffer_27_out, buffer_28_out, buffer_29_out, buffer_30_out, buffer_31_out, buffer_32_out,
       buffer_33_out, buffer_34_out, buffer_35_out, buffer_36_out, buffer_37_out, buffer_38_out,
       buffer_39_out, buffer_40_out, buffer_41_out, buffer_42_out, buffer_43_out, buffer_44_out,
       buffer_45_out, buffer_46_out, buffer_47_out, buffer_48_out, buffer_49_out, buffer_50_out,
       buffer_51_out, buffer_52_out, buffer_53_out, buffer_54_out, buffer_55_out, buffer_56_out,
       buffer_57_out, buffer_58_out, buffer_59_out, buffer_60_out, buffer_61_out, buffer_62_out,
       buffer_63_out, buffer_64_out, buffer_65_out, buffer_66_out, buffer_67_out, buffer_68_out,
       buffer_70_out, or_6_out;

  or or_1 (digit[0], digit1, digit3, digit5, digit7, digit9);
  or or_2 (digit[1], digit2, digit3, 1'b0, digit6, digit7);
  or or_3 (digit[2], digit4, digit5, 1'b0, digit6, digit7);
  or or_4 (digit[3], digit8, digit9);
  or or_5 (isdigit, digit8, digit9, digit7, digit6, digit5, digit4, digit3, digit2, digit1, digit0);
  or or_6 (or_6_out, isdigit, op_star, nop);
  buf buffer_1 (buffer_1_out, buffer_2_out);
  buf buffer_2 (buffer_2_out, buffer_4_out);
  buf buffer_3 (buffer_3_out, or_6_out);
  buf buffer_4 (buffer_4_out, buffer_3_out);
  buf buffer_5 (buffer_5_out, buffer_7_out);
  buf buffer_6 (buffer_6_out, buffer_8_out);
  buf buffer_7 (buffer_7_out, buffer_6_out);
  buf buffer_8 (buffer_8_out, buffer_30_out);
  buf buffer_9 (buffer_9_out, buffer_11_out);
  buf buffer_10 (buffer_10_out, buffer_31_out);
  buf buffer_11 (buffer_11_out, buffer_10_out);
  buf buffer_12 (buffer_12_out, buffer_9_out);
  buf buffer_13 (buffer_13_out, buffer_14_out);
  buf buffer_14 (buffer_14_out, buffer_34_out);
  buf buffer_15 (buffer_15_out, buffer_16_out);
  buf buffer_16 (buffer_16_out, buffer_13_out);
  buf buffer_17 (buffer_17_out, buffer_18_out);
  buf buffer_18 (buffer_18_out, buffer_35_out);
  buf buffer_19 (buffer_19_out, buffer_17_out);
  buf buffer_20 (buffer_20_out, buffer_19_out);
  buf buffer_21 (buffer_21_out, buffer_24_out);
  buf buffer_22 (buffer_22_out, buffer_23_out);
  buf buffer_23 (buffer_23_out, buffer_38_out);
  buf buffer_24 (buffer_24_out, buffer_22_out);
  buf buffer_25 (buffer_25_out, buffer_26_out);
  buf buffer_26 (buffer_26_out, buffer_39_out);
  buf buffer_27 (buffer_27_out, buffer_25_out);
  buf buffer_28 (buffer_28_out, buffer_27_out);
  buf buffer_29 (buffer_29_out, buffer_41_out);
  buf buffer_30 (buffer_30_out, buffer_1_out);
  buf buffer_31 (buffer_31_out, buffer_5_out);
  buf buffer_32 (buffer_32_out, buffer_45_out);
  buf buffer_33 (buffer_33_out, buffer_49_out);
  buf buffer_34 (buffer_34_out, buffer_12_out);
  buf buffer_35 (buffer_35_out, buffer_15_out);
  buf buffer_36 (buffer_36_out, buffer_53_out);
  buf buffer_37 (buffer_37_out, buffer_58_out);
  buf buffer_38 (buffer_38_out, buffer_20_out);
  buf buffer_39 (buffer_39_out, buffer_21_out);
  buf buffer_40 (buffer_40_out, buffer_62_out);
  buf buffer_41 (buffer_41_out, buffer_28_out);
  buf buffer_42 (buffer_42_out, buffer_66_out);
  buf buffer_43 (buffer_43_out, buffer_29_out);
  buf buffer_44 (buffer_44_out, buffer_46_out);
  buf buffer_45 (buffer_45_out, buffer_44_out);
  buf buffer_46 (buffer_46_out, buffer_43_out);
  buf buffer_47 (buffer_47_out, buffer_32_out);
  buf buffer_48 (buffer_48_out, buffer_47_out);
  buf buffer_49 (buffer_49_out, buffer_50_out);
  buf buffer_50 (buffer_50_out, buffer_48_out);
  buf buffer_51 (buffer_51_out, buffer_52_out);
  buf buffer_52 (buffer_52_out, buffer_54_out);
  buf buffer_53 (buffer_53_out, buffer_51_out);
  buf buffer_54 (buffer_54_out, buffer_33_out);
  buf buffer_55 (buffer_55_out, buffer_56_out);
  buf buffer_56 (buffer_56_out, buffer_57_out);
  buf buffer_57 (buffer_57_out, buffer_36_out);
  buf buffer_58 (buffer_58_out, buffer_55_out);
  buf buffer_59 (buffer_59_out, buffer_61_out);
  buf buffer_60 (buffer_60_out, buffer_37_out);
  buf buffer_61 (buffer_61_out, buffer_60_out);
  buf buffer_62 (buffer_62_out, buffer_59_out);
  buf buffer_63 (buffer_63_out, buffer_64_out);
  buf buffer_64 (buffer_64_out, buffer_40_out);
  buf buffer_65 (buffer_65_out, buffer_63_out);
  buf buffer_66 (buffer_66_out, buffer_65_out);
  buf buffer_67 (buffer_67_out, buffer_68_out);
  buf buffer_68 (buffer_68_out, buffer_70_out);
  buf buffer_69 (press, buffer_67_out);
  buf buffer_70 (buffer_70_out, buffer_42_out);

  assign is_star = op_star;
  assign nis = nop;

  // Notes on the sheet:
  //   Keypad
endmodule

module Led16 (
  input  [15:0] in_1,
  output out_2,
  output out_3,
  output out_4,
  output out_5,
  output out_6,
  output out_7,
  output out_8,
  output out_9,
  output out_10,
  output out_11,
  output out_12,
  output out_13,
  output out_14,
  output out_15,
  output out_16,
  output out_17
);


  assign out_2 = in_1[15];
  assign out_3 = in_1[14];
  assign out_4 = in_1[13];
  assign out_5 = in_1[12];
  assign out_6 = in_1[11];
  assign out_7 = in_1[10];
  assign out_8 = in_1[9];
  assign out_9 = in_1[8];
  assign out_10 = in_1[7];
  assign out_11 = in_1[6];
  assign out_12 = in_1[5];
  assign out_13 = in_1[4];
  assign out_14 = in_1[3];
  assign out_15 = in_1[2];
  assign out_16 = in_1[1];
  assign out_17 = in_1[0];

  // Notes on the sheet:
  //   Led16
endmodule
