// Logisim project dragonarch.circ as structural Verilog
module ALU (
  input  [3:0] ALU_code,
  input  [15:0] in_2,
  input  [15:0] in_3,
  output [15:0] out_4
);

  wire adder_1_cout, adder_2_cout, multiplexer_2_out, subtractor_1_bout, subtractor_2_bout, undriven;
  wire [1:0] undriven_2;
  wire [15:0] adder_1_out, adder_2_out, and_1_out, negator_1_out, or_1_out, subtractor_1_out,
       subtractor_2_out, xor_1_out;

  Adder #(.width(16)) adder_1 (.a(in_2), .b(in_2), .out(adder_1_out), .cin(undriven), .cout(adder_1_cout));
  Subtractor #(.width(16)) subtractor_1 (
    .a(in_2), .b(in_2), .out(subtractor_1_out), .bin(undriven), .bout(subtractor_1_bout));
  assign and_1_out = in_2 & in_2;  // AND_Gate and_1, 16 bits wide
  assign or_1_out = in_2 | in_2;  // OR_Gate or_1, 16 bits wide
  assign xor_1_out = in_2 ^ in_2;  // XOR_Gate xor_1, 16 bits wide
  Negator #(.width(16)) negator_1 (.in(in_2), .out(negator_1_out));
  Adder #(.width(16)) adder_2 (.a(in_2), .b(16'h1), .out(adder_2_out), .cin(undriven), .cout(adder_2_cout));
  Subtractor #(.width(16)) subtractor_2 (
    .a(in_2), .b(16'h1), .out(subtractor_2_out), .bin(undriven), .bout(subtractor_2_bout));
  Multiplexer #(.select(4), .width(16), .enable("false")) multiplexer_1 (
    .in0(adder_1_out), .in1(subtractor_1_out), .in2(and_1_out), .in3(or_1_out), .in4(xor_1_out),
    .in5(negator_1_out), .in6(in_2), .in7(adder_2_out), .in8(subtractor_2_out), .out(out_4), .sel(ALU_code));  // open: in9, in10, in11, in12, in13, in14, in15
  Multiplexer #(.select(2), .enable("false")) multiplexer_2 (
    .in0(adder_1_cout), .in1(subtractor_1_bout), .in2(adder_2_cout), .in3(subtractor_2_bout),
    .out(multiplexer_2_out), .sel(undriven_2));

  assign in_3 = in_2;

  // Notes on the sheet:
  //   X
  //   Y
  //   CarryIn???
  //   ???
  //   ???
  //   CarryOut???
endmodule
